# Fritzing sketch testdiagram (saved by Fritzing 0.9.2b)
breadboards: 1

parts:
  Raspberry_Pi1 = Raspberry Pi 2
  R1 = Resistor [tolerance=±5% resistance=470k package=THT]
  LED1 = LED - 3mm [color="Red (633nm)" package="3 mm [THT]"]

nets:
  3V3: Raspberry_Pi1.3v3, Raspberry_Pi1.3V3
  N1: Raspberry_Pi1.GIPO22, R1.Pin_0
  N2: Raspberry_Pi1.GND, LED1.cathode
  N3: R1.Pin_1, LED1.anode
