# Fritzing sketch buzzer-pi (saved by Fritzing 0.9.2b)
circuit board: 11.8403cm x 8.41416cm
breadboards: 1

parts:
  Raspberry_Pi1 = Raspberry Pi 2
  SG1 = Buzzer 12mm [package=buzzer-ccv]
  V1 = DC Power [voltage=5]

nets:
  N1: Raspberry_Pi1.GND, SG1.1, V1.V-
  N2: Raspberry_Pi1.GPIO23, SG1.2
  N3: Raspberry_Pi1.5V, V1.V+
